# Fritzing sketch humtemp (saved by Fritzing 0.9.9b)
perfboards: 1

parts:
  DHT22 = Humidity and Temperature Sensor RHT03
  R1 = Resistor [tolerance=±5% resistance=1M power=0.25 package=THT]
  BAT1 = Battery Holders [package=battery-aa-kit]
  R2 = Resistor [tolerance=±5% resistance=1M power=0.25 package=THT]
  R3 = Resistor [tolerance=±5% resistance=220k power=0.25 package=THT]
  C1 = Electrolytic Capacitor [capacitance=1µF voltage=50V package="0405 [SMD, electrolytic]"]
  R4 = Resistor [tolerance=±5% resistance=10k package="0805 [SMD]"]
  Part2 = Adafruit HUZZAH ESP8266 [part_number="Adafruit #2471"]
  DS1 = DS18B20 1-Wire Temperature Sensor [part_number=DS18B20]
  DS2 = DS18B20 1-Wire Temperature Sensor [part_number=DS18B20]
  DS3 = DS18B20 1-Wire Temperature Sensor [part_number=DS18B20]
  R5 = Resistor [tolerance=±5% resistance=4.7k package="0805 [SMD]"]
  JP2Gnd = Header 1 [package=1x01_offset]
  JP1Bat = Header 1 [package=1x01_offset]

nets:
  VDD: DHT22.Vcc, R4.Pin_1, Part2.3.3V, DS1.VDD, DS2.VDD, DS3.VDD, R5.Pin_0
  N1: DHT22.Data-signal, R4.Pin_0, Part2.GPIO12
  GND: DHT22.GND_2, BAT1.-, R3.Pin_0, C1.-, Part2.GND, DS1.GND, DS2.GND, DS3.GND, JP2Gnd.1
  N2: R1.Pin_0, R2.Pin_1, R3.Pin_1
  N3: R1.Pin_1, BAT1.+, Part2.VBAT, JP1Bat.1
  N4: R2.Pin_0, C1.+, Part2.ADC
  N5: Part2.RESET, Part2.GPIO16
  N6: Part2.GPIO13, DS1.DQ, DS2.DQ, DS3.DQ, R5.Pin_1

custom parts:
  Adafruit HUZZAH ESP8266: Add Internet to your next project with an adorable, bite-sized WiFi microcontroller, at a price you like! The ESP8266 processor from Espressif is an 80 MHz microcontroller with a full WiFi front-end (both as client and access point) and TCP/IP stack with DNS support as well. While this chip has been very popular, its also been very difficult to use. Most of the low cost modules are not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
