# Fritzing sketch humtemp_V2 (saved by Fritzing 0.9.9b)
perfboards: 1

parts:
  RHT1 = Humidity and Temperature Sensor RHT03
  BAT1 = Battery Holders [package=battery-aa-kit]
  R5 = Resistor [tolerance=±5% resistance=220k power=0.25 package=THT]
  C2 = Electrolytic Capacitor [capacitance=0.47nF voltage=50V package="0405 [SMD, electrolytic]"]
  ESP8266_Huzzah = Adafruit HUZZAH ESP8266 [part_number="Adafruit #2471"]
  DS3 = DS18B20 1-Wire Temperature Sensor [part_number=DS18B20]
  DS1 = DS18B20 1-Wire Temperature Sensor [part_number=DS18B20]
  DS2 = DS18B20 1-Wire Temperature Sensor [part_number=DS18B20]
  R3 = Resistor [tolerance=±5% resistance=4.7k package="0805 [SMD]"]
  JP1 = Header 1 [package=1x01_offset]
  JP2 = Header 1 [package=1x01_offset]
  R4 = Resistor [tolerance=±5% resistance=10k power=0.25 package=THT]
  R2 = Resistor [tolerance=±5% resistance=1M power=0.25 package=THT]
  R1 = Resistor [tolerance=±5% power=0.25 resistance=1M package=THT]

nets:
  VDD: RHT1.Vcc, ESP8266_Huzzah.3.3V, DS3.VDD, DS1.VDD, DS2.VDD, R3.Pin_0, R4.Pin_1
  N1: RHT1.Data-signal, ESP8266_Huzzah.GPIO12, R4.Pin_0
  GND: RHT1.GND_2, BAT1.-, R5.Pin_0, C2.-, ESP8266_Huzzah.GND, DS3.GND, DS1.GND, DS2.GND, JP1.1
  N2: BAT1.+, C2.+, ESP8266_Huzzah.ADC, ESP8266_Huzzah.VBAT, JP2.1, R2.Pin_0, R1.Pin_1
  N3: R5.Pin_1, R2.Pin_1, R1.Pin_0
  N4: ESP8266_Huzzah.RESET, ESP8266_Huzzah.GPIO16
  N5: ESP8266_Huzzah.GPIO13, DS3.DQ, DS1.DQ, DS2.DQ, R3.Pin_1

custom parts:
  Adafruit HUZZAH ESP8266: Add Internet to your next project with an adorable, bite-sized WiFi microcontroller, at a price you like! The ESP8266 processor from Espressif is an 80 MHz microcontroller with a full WiFi front-end (both as client and access point) and TCP/IP stack with DNS support as well. While this chip has been very popular, its also been very difficult to use. Most of the low cost modules are not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
